// Logisim project 1.circ as structural Verilog: 3 circuits, main circuit main
module main (
  input  A,
  input  B,
  input  C,
  input  D,
  output P
);

  wire n7404_1__2__1y, n74151_1__5__y, n74151_1__6__w, not_1_out;

  and and_1 (P, n74151_1__5__y, not_1_out);
  _7404 u_7404_1 (
    ._1__1A(D), ._2__1Y(n7404_1__2__1y), ._7__GND(1'b0), ._14__Vcc(1'b1));  // open: _3__2A, _4__2Y, _5__3A, _6__3Y, _13__6A, _12__6Y, _11__5A, _10__5Y, _9__4A, _8__4Y
  not not_1 (not_1_out, n74151_1__6__w);
  _74151 u_74151_1 (
    ._1__D3(D), ._2__D2(n7404_1__2__1y), ._3__D1(n7404_1__2__1y), ._4__D0(D), ._5__Y(n74151_1__5__y),
    ._6__W(n74151_1__6__w), ._7__nG(1'b0), ._8__GND(1'b0), ._16__Vcc(1'b1), ._15__D4(n7404_1__2__1y),
    ._14__D5(D), ._13__D6(D), ._12__D7(n7404_1__2__1y), ._11__A(A), ._10__B(B), ._9__C(C));
endmodule

module _74151 (
  input  _1__D3,
  input  _16__Vcc,
  input  _2__D2,
  input  _15__D4,
  input  _3__D1,
  input  _14__D5,
  input  _4__D0,
  input  _13__D6,
  input  _12__D7,
  input  _11__A,
  input  _7__nG,
  input  _10__B,
  input  _8__GND,
  input  _9__C,
  output _5__Y,
  output _6__W
);

  wire multiplexer_1_out, not_2_out;

  not not_1 (_5__Y, _6__W);
  or or_1 (_6__W, not_2_out, _7__nG);
  not not_2 (not_2_out, multiplexer_1_out);
  Multiplexer #(.select(3), .enable("false")) multiplexer_1 (
    .in0(_4__D0), .in1(_3__D1), .in2(_2__D2), .in3(_1__D3), .in4(_15__D4), .in5(_14__D5), .in6(_13__D6),
    .in7(_12__D7), .out(multiplexer_1_out), .sel({_9__C, _10__B, _11__A}));

  // Notes on the sheet:
  //   74151: 8-Line to 1-Line Multiplexer
endmodule

module _7404 (
  input  _1__1A,
  input  _14__Vcc,
  input  _13__6A,
  input  _3__2A,
  input  _11__5A,
  input  _5__3A,
  input  _9__4A,
  input  _7__GND,
  output _2__1Y,
  output _12__6Y,
  output _4__2Y,
  output _10__5Y,
  output _6__3Y,
  output _8__4Y
);

  not not_1 (_2__1Y, _1__1A);
  not not_2 (_4__2Y, _3__2A);
  not not_3 (_6__3Y, _5__3A);
  not not_4 (_12__6Y, _13__6A);
  not not_5 (_10__5Y, _11__5A);
  not not_6 (_8__4Y, _9__4A);

  // Notes on the sheet:
  //   7407: hex inverter
endmodule
