// Logisim project 2.circ as structural Verilog: 1 circuit, main circuit main
module main (
  input  A,
  input  B,
  input  C,
  input  D,
  output P
);

  wire not_1_out, xor_1_out;

  not not_1 (not_1_out, xor_1_out);
  Multiplexer #(.select(2), .enable("false")) multiplexer_1 (
    .in0(xor_1_out), .in1(not_1_out), .in2(not_1_out), .in3(xor_1_out), .out(P), .sel({A, B}));
  xor xor_1 (xor_1_out, C, D);
endmodule
