// Logisim project 3.circ as structural Verilog: 3 circuits, main circuit main
module main (
  input  A,
  input  B,
  output Z1,
  output Z2
);

  wire n74154_1__1__y0, n74154_1__2__y1, n74154_1__3__y2, n74154_1__4__y3, n74154_1__5__y4, n74154_1__6__y5,
       n74154_1__7__y6, n74154_1__8__y7, n74154_1__9__y8, n74154_1__10__y9, n74154_1__11__y10,
       n74154_1__13__y11, n74154_1__14__y12, n74154_1__15__y13, n74154_1__16__y14, n74154_1__17__y15;

  _7430 u_7430_1 (
    ._1__1A(n74154_1__11__y10), ._2__1B(n74154_1__9__y8), ._3__1C(n74154_1__8__y7), ._4__1D(n74154_1__6__y5),
    ._5__1E(n74154_1__3__y2), ._6__1F(n74154_1__1__y0), ._7__GND(1'b0), ._14__Vcc(1'b1),
    ._12__1H(n74154_1__15__y13), ._11__1G(n74154_1__17__y15), ._8__3Y(Z2));  // open: _13__NC, _10__NC, _9__NC
  _7430 u_7430_2 (
    ._1__1A(n74154_1__13__y11), ._2__1B(n74154_1__10__y9), ._3__1C(n74154_1__7__y6),
    ._4__1D(n74154_1__5__y4), ._5__1E(n74154_1__4__y3), ._6__1F(n74154_1__2__y1), ._7__GND(1'b0),
    ._14__Vcc(1'b1), ._12__1H(n74154_1__14__y12), ._11__1G(n74154_1__16__y14), ._8__3Y(Z1));  // open: _13__NC, _10__NC, _9__NC
  _74154 u_74154_1 (
    ._1__Y0(n74154_1__1__y0), ._2__Y1(n74154_1__2__y1), ._3__Y2(n74154_1__3__y2), ._4__Y3(n74154_1__4__y3),
    ._5__Y4(n74154_1__5__y4), ._6__Y5(n74154_1__6__y5), ._7__Y6(n74154_1__7__y6), ._8__Y7(n74154_1__8__y7),
    ._9__Y8(n74154_1__9__y8), ._10__Y9(n74154_1__10__y9), ._11__Y10(n74154_1__11__y10), ._12__GND(1'b0),
    ._24__Vcc(1'b1), ._23__A(A), ._22__B(A), ._21__C(B), ._20__D(B), ._19__G2(1'b0), ._18__G1(1'b0),
    ._17__Y15(n74154_1__17__y15), ._16__Y14(n74154_1__16__y14), ._15__Y13(n74154_1__15__y13),
    ._14__Y12(n74154_1__14__y12), ._13__Y11(n74154_1__13__y11));
endmodule

module _74154 (
  input  _24__Vcc,
  input  _23__A,
  input  _22__B,
  input  _21__C,
  input  _20__D,
  input  _19__G2,
  input  _18__G1,
  input  _12__GND,
  output _1__Y0,
  output _2__Y1,
  output _3__Y2,
  output _4__Y3,
  output _5__Y4,
  output _6__Y5,
  output _7__Y6,
  output _8__Y7,
  output _17__Y15,
  output _9__Y8,
  output _16__Y14,
  output _10__Y9,
  output _15__Y13,
  output _11__Y10,
  output _14__Y12,
  output _13__Y11
);

  wire and_12_out, decoder_1_out0, decoder_1_out1, decoder_1_out2, decoder_1_out3, decoder_1_out4,
       decoder_1_out5, decoder_1_out6, decoder_1_out7, decoder_1_out8, decoder_1_out9, decoder_1_out10,
       decoder_1_out11, decoder_1_out12, decoder_1_out13, decoder_1_out14, decoder_1_out15, not_1_out,
       not_2_out, not_3_out, not_4_out, not_5_out, not_6_out, not_7_out, not_8_out, not_9_out, not_10_out,
       not_11_out, not_12_out, not_13_out, not_14_out, not_15_out, not_16_out, not_17_out, not_18_out;

  not not_1 (not_1_out, decoder_1_out0);
  and and_1 (_1__Y0, not_1_out, and_12_out);
  not not_2 (not_2_out, decoder_1_out1);
  and and_2 (_2__Y1, not_2_out, and_12_out);
  not not_3 (not_3_out, decoder_1_out2);
  and and_3 (_3__Y2, not_3_out, and_12_out);
  not not_4 (not_4_out, decoder_1_out3);
  and and_4 (_4__Y3, not_4_out, and_12_out);
  not not_5 (not_5_out, decoder_1_out4);
  and and_5 (_5__Y4, not_5_out, and_12_out);
  not not_6 (not_6_out, decoder_1_out5);
  and and_6 (_6__Y5, not_6_out, and_12_out);
  not not_7 (not_7_out, decoder_1_out6);
  and and_7 (_7__Y6, not_7_out, and_12_out);
  not not_8 (not_8_out, decoder_1_out7);
  and and_8 (_8__Y7, not_8_out, and_12_out);
  not not_9 (not_9_out, decoder_1_out8);
  and and_9 (_9__Y8, not_9_out, and_12_out);
  not not_10 (not_10_out, decoder_1_out9);
  and and_10 (_10__Y9, not_10_out, and_12_out);
  not not_11 (not_11_out, decoder_1_out10);
  and and_11 (_11__Y10, not_11_out, and_12_out);
  and and_12 (and_12_out, not_12_out, not_13_out);
  Decoder #(.select(4), .enable("false")) decoder_1 (
    .out0(decoder_1_out0), .out1(decoder_1_out1), .out2(decoder_1_out2), .out3(decoder_1_out3),
    .out4(decoder_1_out4), .out5(decoder_1_out5), .out6(decoder_1_out6), .out7(decoder_1_out7),
    .out8(decoder_1_out8), .out9(decoder_1_out9), .out10(decoder_1_out10), .out11(decoder_1_out11),
    .out12(decoder_1_out12), .out13(decoder_1_out13), .out14(decoder_1_out14), .out15(decoder_1_out15),
    .sel({_20__D, _21__C, _22__B, _23__A}));
  not not_12 (not_12_out, _19__G2);
  not not_13 (not_13_out, _18__G1);
  not not_14 (not_14_out, decoder_1_out15);
  and and_13 (_17__Y15, not_14_out, and_12_out);
  not not_15 (not_15_out, decoder_1_out14);
  and and_14 (_16__Y14, not_15_out, and_12_out);
  not not_16 (not_16_out, decoder_1_out13);
  and and_15 (_15__Y13, not_16_out, and_12_out);
  not not_17 (not_17_out, decoder_1_out12);
  and and_16 (_14__Y12, not_17_out, and_12_out);
  not not_18 (not_18_out, decoder_1_out11);
  and and_17 (_13__Y11, not_18_out, and_12_out);

  // Notes on the sheet:
  //   74154: 4-Line to 16-Line Decoder
endmodule

module _7430 (
  input  _1__1A,
  input  _14__Vcc,
  input  _2__1B,
  input  _13__NC,
  input  _3__1C,
  input  _12__1H,
  input  _4__1D,
  input  _11__1G,
  input  _5__1E,
  input  _10__NC,
  input  _6__1F,
  input  _9__NC,
  input  _7__GND,
  output _8__3Y
);

  nand nand_1 (_8__3Y, _6__1F, _5__1E, _4__1D, _3__1C, _2__1B, _1__1A, _12__1H, _11__1G);

  // Notes on the sheet:
  //   7430: 8-input NAND 
endmodule
