// Logisim project 1.circ as structural Verilog: 1 circuit, main circuit Half Adder
module Half_Adder (
  input  A,
  input  B,
  output Sum,
  output C_out
);

  wire nand_1_out;

  xor xor_1 (Sum, A, B);
  nand nand_1 (nand_1_out, A, B);
  nand nand_2 (C_out, nand_1_out, nand_1_out);
endmodule
