// Logisim project 2.circ as structural Verilog: 3 circuits, main circuit main
module main (
  input  A4__8,
  input  A3__4,
  input  A2__2,
  input  A1__1,
  input  B4__8,
  input  B3__4,
  input  B2__2,
  input  B1__1,
  input  M__0,
  output out_10,
  output S4__1,
  output S3__2,
  output S2__4,
  output S1__8
);

  wire n7486_1__3__1y, n7486_1__6__2y, n7486_1__8__3y, n7486_1__11__4y;

  _7486 u_7486_1 (
    ._1__1A(B1__1), ._2__1B(M__0), ._3__1Y(n7486_1__3__1y), ._4__2A(B2__2), ._5__2B(M__0),
    ._6__2Y(n7486_1__6__2y), ._7__GND(1'b0), ._14__Vcc(1'b1), ._13__4B(M__0), ._12__4A(B4__8),
    ._11__4Y(n7486_1__11__4y), ._10__3B(M__0), ._9__3A(B3__4), ._8__3Y(n7486_1__8__3y));
  _7483 u_7483_1 (
    ._1__A4(A4__8), ._2__S3(S2__4), ._3__A3(A3__4), ._4__B3(n7486_1__8__3y), ._5__Vcc(1'b1), ._6__S2(S3__2),
    ._7__B2(n7486_1__6__2y), ._8__A2(A2__2), ._16__B4(n7486_1__11__4y), ._15__S4(S1__8), ._14__Cout(out_10),
    ._13__Cin(M__0), ._12__GND(1'b0), ._11__B1(n7486_1__3__1y), ._10__A1(A1__1), ._9__S1(S4__1));
endmodule

module _7483 (
  input  _1__A4,
  input  _16__B4,
  input  _3__A3,
  input  _4__B3,
  input  _13__Cin,
  input  _5__Vcc,
  input  _12__GND,
  input  _11__B1,
  input  _7__B2,
  input  _10__A1,
  input  _8__A2,
  output _2__S3,
  output _15__S4,
  output _14__Cout,
  output _6__S2,
  output _9__S1
);

  wire and_1_out, and_2_out, and_3_out, and_4_out, and_5_out, and_6_out, and_7_out, and_8_out, and_9_out,
       and_10_out, and_11_out, and_12_out, and_13_out, and_14_out, nand_1_out, nand_2_out, nand_3_out,
       nand_4_out, nor_1_out, nor_2_out, nor_3_out, nor_4_out, nor_6_out, nor_7_out, nor_8_out, not_1_out,
       not_2_out, not_3_out, not_4_out, not_5_out, not_6_out;

  nand nand_1 (nand_1_out, _16__B4, _1__A4);
  nor nor_1 (nor_1_out, _16__B4, _1__A4);
  nand nand_2 (nand_2_out, _4__B3, _3__A3);
  nor nor_2 (nor_2_out, _4__B3, _3__A3);
  nand nand_3 (nand_3_out, _7__B2, _8__A2);
  nor nor_3 (nor_3_out, _7__B2, _8__A2);
  nand nand_4 (nand_4_out, _11__B1, _10__A1);
  nor nor_4 (nor_4_out, _11__B1, _10__A1);
  and and_1 (and_1_out, nor_2_out, nand_1_out);
  and and_2 (and_2_out, nor_3_out, nand_1_out, nand_2_out);
  and and_3 (and_3_out, nor_4_out, nand_1_out, nand_2_out, nand_3_out);
  and and_4 (and_4_out, nand_1_out, nand_2_out, nand_3_out, nand_4_out, not_2_out);
  not not_1 (not_1_out, nor_1_out);
  and and_5 (and_5_out, nor_3_out, nand_2_out);
  and and_6 (and_6_out, nor_4_out, nand_2_out, nand_3_out);
  and and_7 (and_7_out, nand_2_out, nand_3_out, nand_4_out, not_2_out);
  not not_2 (not_2_out, _13__Cin);
  not not_3 (not_3_out, nor_2_out);
  and and_8 (and_8_out, nor_4_out, nand_3_out);
  and and_9 (and_9_out, nand_3_out, nand_4_out, not_2_out);
  not not_4 (not_4_out, nor_3_out);
  and and_10 (and_10_out, nand_4_out, not_2_out);
  not not_5 (not_5_out, nor_4_out);
  not not_6 (not_6_out, not_2_out);
  nor nor_5 (_14__Cout, nor_1_out, and_1_out, and_2_out, and_3_out, and_4_out);
  and and_11 (and_11_out, nand_1_out, not_1_out);
  and and_12 (and_12_out, nand_2_out, not_3_out);
  and and_13 (and_13_out, nand_3_out, not_4_out);
  and and_14 (and_14_out, nand_4_out, not_5_out);
  xor xor_1 (_15__S4, and_11_out, nor_6_out);
  nor nor_6 (nor_6_out, nor_2_out, and_5_out, and_6_out, and_7_out);
  xor xor_2 (_2__S3, and_12_out, nor_7_out);
  nor nor_7 (nor_7_out, nor_3_out, and_8_out, and_9_out);
  xor xor_3 (_6__S2, and_13_out, nor_8_out);
  nor nor_8 (nor_8_out, nor_4_out, and_10_out);
  xor xor_4 (_9__S1, and_14_out, not_6_out);
endmodule

module _7486 (
  input  _1__1A,
  input  _14__Vcc,
  input  _2__1B,
  input  _13__4B,
  input  _12__4A,
  input  _4__2A,
  input  _5__2B,
  input  _10__3B,
  input  _9__3A,
  input  _7__GND,
  output _3__1Y,
  output _11__4Y,
  output _6__2Y,
  output _8__3Y
);

  xor xor_1 (_3__1Y, _2__1B, _1__1A);
  xor xor_2 (_6__2Y, _5__2B, _4__2A);
  xor xor_3 (_11__4Y, _13__4B, _12__4A);
  xor xor_4 (_8__3Y, _10__3B, _9__3A);
endmodule
