// Logisim project lab5 (1).circ as structural Verilog: 1 circuit, main circuit main
module main (
  input  S,
  input  C,
  input  R,
  output Q,
  output Q_prime
);

  wire nand_1_out, nand_2_out;

  nand nand_1 (nand_1_out, S, C);
  nand nand_2 (nand_2_out, C, R);
  nand nand_3 (Q, nand_1_out, Q_prime);
  nand nand_4 (Q_prime, Q, nand_2_out);

  // Notes on the sheet:
  //   C: pull=down
  //   Öncelikle devrenin tüm pinlerinin bir defa açılması gerekmektedir
endmodule
