// Logisim project lab5 (3).circ as structural Verilog: 3 circuits, main circuit main
module main (
  input  Preset1,
  input  J1,
  input  K1,
  input  Clear1,
  output Q1,
  output Q_prime_1
);

  wire Clock1_out;

  Clock Clock1 (.out(Clock1_out));
  _7476 u_7476_1 (
    .Vcc(1'b1), .Preset1(Preset1), .J1(J1), .Clock1(Clock1_out), .K1(K1), .Clear1(Clear1), .Gnd(1'b0),
    .Q1(Q1), .Q1_prime(Q_prime_1));  // open: Preset2, J2, Clock2, K2, Clear2, Q2, Q2_prime
endmodule

module _7476 (
  input  Vcc,
  input  Preset1,
  input  J1,
  input  Clock1,
  input  K1,
  input  Clear1,
  input  Preset2,
  input  J2,
  input  Clock2,
  input  K2,
  input  Clear2,
  input  Gnd,
  output Q1,
  output Q1_prime,
  output Q2,
  output Q2_prime
);

  J_K_Flip_Flop j_k_flip_flop_1 (
    .Preset(Preset1), .J(J1), .Clock(Clock1), .K(K1), .Clear(Clear1), .Q(Q1), .Q_prime(Q1_prime));
  J_K_Flip_Flop j_k_flip_flop_2 (
    .Preset(Preset2), .J(J2), .Clock(Clock2), .K(K2), .Clear(Clear2), .Q(Q2), .Q_prime(Q2_prime));
endmodule

module J_K_Flip_Flop (
  input  Preset,
  input  J,
  input  Clock,
  input  K,
  input  Clear,
  output Q,
  output Q_prime
);

  wire nand_1_out, nand_2_out, nand_3_out, nand_4_out, nand_5_out, nand_6_out, not_1_out;

  nand nand_1 (nand_1_out, J, Clock);
  nand nand_2 (nand_2_out, Clock, K);
  not not_1 (not_1_out, Clock);
  nand nand_3 (nand_3_out, Preset, nand_1_out, nand_4_out);
  nand nand_4 (nand_4_out, nand_3_out, nand_2_out, Clear);
  nand nand_5 (nand_5_out, nand_3_out, not_1_out);
  nand nand_6 (nand_6_out, not_1_out, nand_4_out);
  nand nand_7 (Q, Preset, nand_5_out, Q_prime);
  nand nand_8 (Q_prime, Q, nand_6_out, Clear);
endmodule
